// Logisim project LC3-2200a.circ as structural Verilog: 2 circuits, main circuit my circuit
module my_circuit (
);

  wire and_1_out, and_2_out, and_3_out, and_4_out, and_5_out, and_6_out, and_7_out, and_8_out, and_9_out,
       and_10_out, and_11_out, and_12_out, and_13_out, and_14_out, and_15_out, and_16_out, Clock,
       decoder_1_out0, decoder_1_out1, decoder_1_out2, decoder_1_out3, decoder_1_out4, decoder_1_out5,
       decoder_1_out6, decoder_1_out7, decoder_1_out8, decoder_1_out9, decoder_1_out10, decoder_1_out11,
       decoder_1_out12, decoder_1_out13, decoder_1_out14, decoder_1_out15, undriven_2, undriven_4,
       undriven_5, undriven_6, undriven_7, undriven_8, undriven_9, undriven_10, undriven_11, undriven_12,
       undriven_13, undriven_14, undriven_15, undriven_16, undriven_17, undriven_18, undriven_19,
       undriven_20, WrReg;
  wire [3:0] RegNo;
  wire [31:0] multiplexer_1_out, register_2_q, register_3_q, register_4_q, register_5_q, register_6_q,
       register_7_q, register_8_q, register_9_q, register_10_q, register_11_q, register_12_q, register_13_q,
       register_14_q, register_15_q, register_16_q, register_17_q, register_18_q, register_19_q, undriven,
       undriven_3;

  Register register_1 ();  // open: D, en, Q, clk, clr
  Register #(.width(32)) register_2 (.D(undriven), .en(undriven_2), .Q(register_2_q));  // open: clk, clr
  Register #(.width(32)) register_3 (.D(undriven_3), .en(undriven_4), .Q(register_3_q));  // open: clk, clr
  Decoder #(.select(4), .enable("false")) decoder_1 (
    .out0(decoder_1_out0), .out1(decoder_1_out1), .out2(decoder_1_out2), .out3(decoder_1_out3),
    .out4(decoder_1_out4), .out5(decoder_1_out5), .out6(decoder_1_out6), .out7(decoder_1_out7),
    .out8(decoder_1_out8), .out9(decoder_1_out9), .out10(decoder_1_out10), .out11(decoder_1_out11),
    .out12(decoder_1_out12), .out13(decoder_1_out13), .out14(decoder_1_out14), .out15(decoder_1_out15),
    .sel(RegNo));
  and and_1 (and_1_out, decoder_1_out0, WrReg);
  and and_2 (and_2_out, decoder_1_out1, WrReg);
  and and_3 (and_3_out, decoder_1_out2, WrReg);
  and and_4 (and_4_out, decoder_1_out3, WrReg);
  and and_5 (and_5_out, decoder_1_out4, WrReg);
  and and_6 (and_6_out, decoder_1_out5, WrReg);
  and and_7 (and_7_out, decoder_1_out6, WrReg);
  and and_8 (and_8_out, decoder_1_out7, WrReg);
  and and_9 (and_9_out, decoder_1_out8, WrReg);
  and and_10 (and_10_out, decoder_1_out9, WrReg);
  and and_11 (and_11_out, decoder_1_out10, WrReg);
  and and_12 (and_12_out, decoder_1_out11, WrReg);
  and and_13 (and_13_out, decoder_1_out12, WrReg);
  and and_14 (and_14_out, decoder_1_out13, WrReg);
  and and_15 (and_15_out, decoder_1_out14, WrReg);
  and and_16 (and_16_out, decoder_1_out15, WrReg);
  Register #(.width(32)) register_4 (.en(and_1_out), .Q(register_4_q), .clk(Clock), .clr(undriven_5));  // open: D
  Register #(.width(32)) register_5 (.en(and_2_out), .Q(register_5_q), .clk(Clock), .clr(undriven_6));  // open: D
  Register #(.width(32)) register_6 (.en(and_3_out), .Q(register_6_q), .clk(Clock), .clr(undriven_7));  // open: D
  Register #(.width(32)) register_7 (.en(and_4_out), .Q(register_7_q), .clk(Clock), .clr(undriven_8));  // open: D
  Register #(.width(32)) register_8 (.en(and_5_out), .Q(register_8_q), .clk(Clock), .clr(undriven_9));  // open: D
  Register #(.width(32)) register_9 (.en(and_6_out), .Q(register_9_q), .clk(Clock), .clr(undriven_10));  // open: D
  Register #(.width(32)) register_10 (.en(and_7_out), .Q(register_10_q), .clk(Clock), .clr(undriven_11));  // open: D
  Register #(.width(32)) register_11 (.en(and_8_out), .Q(register_11_q), .clk(Clock), .clr(undriven_12));  // open: D
  Register #(.width(32)) register_12 (.en(and_9_out), .Q(register_12_q), .clk(Clock), .clr(undriven_13));  // open: D
  Register #(.width(32)) register_13 (.en(and_10_out), .Q(register_13_q), .clk(Clock), .clr(undriven_14));  // open: D
  Register #(.width(32)) register_14 (.en(and_11_out), .Q(register_14_q), .clk(Clock), .clr(undriven_15));  // open: D
  Register #(.width(32)) register_15 (.en(and_12_out), .Q(register_15_q), .clk(Clock), .clr(undriven_16));  // open: D
  Register #(.width(32)) register_16 (.en(and_13_out), .Q(register_16_q), .clk(Clock), .clr(undriven_17));  // open: D
  Register #(.width(32)) register_17 (.en(and_14_out), .Q(register_17_q), .clk(Clock), .clr(undriven_18));  // open: D
  Register #(.width(32)) register_18 (.en(and_15_out), .Q(register_18_q), .clk(Clock), .clr(undriven_19));  // open: D
  Register #(.width(32)) register_19 (.en(and_16_out), .Q(register_19_q), .clk(Clock), .clr(undriven_20));  // open: D
  Multiplexer #(.select(4), .width(32), .disabled(0), .enable("false")) multiplexer_1 (
    .in0(register_4_q), .in1(register_5_q), .in2(register_6_q), .in3(register_7_q), .in4(register_8_q),
    .in5(register_9_q), .in6(register_10_q), .in7(register_11_q), .in8(register_12_q), .in9(register_13_q),
    .in10(register_14_q), .in11(register_15_q), .in12(register_16_q), .in13(register_17_q),
    .in14(register_18_q), .in15(register_19_q), .out(multiplexer_1_out), .sel(RegNo));

  // Notes on the sheet:
  //   $zero
  //   $at
  //   $v0
  //   $a1
  //   $a2
  //   $t0
  //   $t1
  //   $t2
  //   $s1
  //   $s2
  //   $k0
  //   $sp
  //   $fp
  //   $ra
endmodule

module Registers (
);

  wire undriven, undriven_2, undriven_3, undriven_4, undriven_5, undriven_6, undriven_12, undriven_24,
       undriven_25, undriven_26, undriven_27, undriven_28, undriven_29, undriven_30;
  wire [7:0] register_1_q, register_2_q, register_3_q, register_4_q, register_5_q, register_6_q,
       register_7_q, register_8_q, register_9_q, register_10_q, register_11_q, register_12_q, register_13_q,
       register_14_q, register_15_q, register_16_q, undriven_7, undriven_8, undriven_9, undriven_10,
       undriven_11, undriven_13, undriven_14, undriven_15, undriven_16, undriven_17, undriven_18,
       undriven_19, undriven_20, undriven_21, undriven_22, undriven_23;

  Register register_1 (.D(undriven_7), .en(undriven), .Q(register_1_q), .clk(undriven_24), .clr(undriven_26));
  Register register_2 (.D(undriven_8), .en(undriven_2), .Q(register_2_q), .clk(undriven_25), .clr(undriven_27));
  Register register_3 (.D(undriven_9), .en(undriven_3), .Q(register_3_q), .clr(undriven_28));  // open: clk
  Register register_4 (.D(undriven_10), .en(undriven_4), .Q(register_4_q), .clk(undriven_6), .clr(undriven_29));
  Register register_5 (.D(undriven_11), .en(undriven_5), .Q(register_5_q), .clk(undriven_12), .clr(undriven_30));
  Register register_6 (.D(undriven_13), .Q(register_6_q));  // open: en, clk, clr
  Register register_7 (.D(undriven_14), .Q(register_7_q));  // open: en, clk, clr
  Register register_8 (.D(undriven_15), .Q(register_8_q));  // open: en, clk, clr
  Register register_9 (.D(undriven_16), .Q(register_9_q));  // open: en, clk, clr
  Register register_10 (.D(undriven_17), .Q(register_10_q));  // open: en, clk, clr
  Register register_11 (.D(undriven_18), .Q(register_11_q));  // open: en, clk, clr
  Register register_12 (.D(undriven_19), .Q(register_12_q));  // open: en, clk, clr
  Register register_13 (.D(undriven_20), .Q(register_13_q));  // open: en, clk, clr
  Register register_14 (.D(undriven_21), .Q(register_14_q));  // open: en, clk, clr
  Register register_15 (.D(undriven_22), .Q(register_15_q));  // open: en, clk, clr
  Register register_16 (.D(undriven_23), .Q(register_16_q));  // open: en, clk, clr

  // Notes on the sheet:
  //   $zero
  //   $at
  //   $v0
  //   $a0
  //   $a1
  //   $a2
  //   $t0
  //   $t1
  //   $t2
  //   $s0
  //   $s1
  //   $s2
  //   $k0
  //   $sp
  //   $fp
  //   $ra
endmodule
